// Logisim project alu_sketch.circ as structural Verilog: 1 circuit, main circuit main
module main (
);

  wire nand_2_out, nand_4_out, nand_5_out, nand_6_out, nand_7_out, nand_8_out, nand_9_out, nand_10_out,
       nand_11_out, nand_12_out, nand_13_out, nand_14_out, nand_15_out, nand_16_out, nand_17_out,
       nand_18_out, nand_19_out, nand_20_out, transistor_1_out, transistor_2_out, undriven, undriven_2,
       undriven_3, undriven_4, undriven_5, undriven_6;

  // NAND_Gate nand_1 is placed but not wired
  nand nand_2 (nand_2_out, 1'b0, 1'b0);
  Transistor #(.\type ("n")) transistor_1 (.in(1'b1), .out(transistor_1_out), .gate(nand_2_out));
  Transistor #(.\type ("n")) transistor_2 (.in(1'b1), .out(transistor_2_out), .gate(1'b0));
  nand nand_3 (transistor_1_out, transistor_2_out, transistor_2_out);
  nand nand_4 (nand_4_out, undriven, undriven_4);
  nand nand_5 (nand_5_out, undriven_2, undriven_5);
  nand nand_6 (nand_6_out, 1'b1, 1'b1);
  nand nand_7 (nand_7_out, 1'b1, transistor_1_out);
  nand nand_8 (nand_8_out, undriven_3, undriven_6);
  nand nand_9 (nand_9_out, undriven, nand_4_out);
  nand nand_10 (nand_10_out, nand_4_out, undriven_4);
  nand nand_11 (nand_11_out, undriven_2, nand_5_out);
  nand nand_12 (nand_12_out, nand_5_out, undriven_5);
  nand nand_13 (nand_13_out, 1'b1, nand_6_out);
  nand nand_14 (nand_14_out, nand_6_out, 1'b1);
  nand nand_15 (nand_15_out, undriven_3, nand_8_out);
  nand nand_16 (nand_16_out, nand_8_out, undriven_6);
  nand nand_17 (nand_17_out, nand_9_out, nand_10_out);
  nand nand_18 (nand_18_out, nand_11_out, nand_12_out);
  nand nand_19 (nand_19_out, nand_13_out, nand_14_out);
  nand nand_20 (nand_20_out, nand_15_out, nand_16_out);
endmodule
