// Logisim project machine.circ as structural Verilog: 4 circuits, main circuit main
module main (
);

  wire clock_1_out, clock_2_out;
  wire [7:0] controlled_buffer_2_out, counter_1_q, register_1_q, register_2_q, rom_1_data;

  Clock clock_1 (.out(clock_1_out));
  Clock clock_2 (.out(clock_2_out));
  Counter counter_1 (.Q(counter_1_q), .clk(clock_1_out), .clr(clock_2_out));  // open: load, D, count, carry
  LED led_1 (.in(register_1_q[0]));
  LED led_2 (.in(register_1_q[1]));
  LED led_3 (.in(register_1_q[2]));
  LED led_4 (.in(register_1_q[3]));
  LED led_5 (.in(register_1_q[4]));
  LED led_6 (.in(register_1_q[5]));
  LED led_7 (.in(register_1_q[6]));
  LED led_8 (.in(register_1_q[7]));
  ROM rom_1 (.addr(counter_1_q), .data(rom_1_data), .sel(1'b1));
  Register register_1 (
    .D(controlled_buffer_2_out), .en(rom_1_data[5]), .Q(register_1_q), .clk(clock_1_out));  // open: clr
  assign controlled_buffer_2_out[3] = 1'b0 ? 1'b1 : 1'bz;  // Controlled_Buffer controlled_buffer_1
  assign controlled_buffer_2_out[0] = 1'b0 ? 1'b0 : 1'bz;  // Controlled_Buffer controlled_buffer_2
  assign controlled_buffer_2_out[1] = 1'b0 ? 1'b1 : 1'bz;  // Controlled_Buffer controlled_buffer_3
  assign controlled_buffer_2_out[2] = 1'b0 ? 1'b0 : 1'bz;  // Controlled_Buffer controlled_buffer_4
  Register register_2 (
    .D(controlled_buffer_2_out), .en(rom_1_data[3]), .Q(register_2_q), .clk(clock_1_out));  // open: clr
  assign controlled_buffer_2_out[7] = 1'b0 ? 1'b1 : 1'bz;  // Controlled_Buffer controlled_buffer_5
  assign controlled_buffer_2_out[5] = 1'b0 ? 1'b0 : 1'bz;  // Controlled_Buffer controlled_buffer_6
  assign controlled_buffer_2_out[6] = 1'b0 ? 1'b1 : 1'bz;  // Controlled_Buffer controlled_buffer_7
  assign controlled_buffer_2_out[4] = 1'b0 ? 1'b1 : 1'bz;  // Controlled_Buffer controlled_buffer_8
  assign controlled_buffer_2_out[1] = rom_1_data[4] ? register_2_q[0] : 1'bz;  // Controlled_Buffer controlled_buffer_9
  assign controlled_buffer_2_out[0] = rom_1_data[4] ? register_2_q[1] : 1'bz;  // Controlled_Buffer controlled_buffer_10
  assign controlled_buffer_2_out[2] = rom_1_data[4] ? register_2_q[2] : 1'bz;  // Controlled_Buffer controlled_buffer_11
  assign controlled_buffer_2_out[3] = rom_1_data[4] ? register_2_q[3] : 1'bz;  // Controlled_Buffer controlled_buffer_12
  assign controlled_buffer_2_out[4] = rom_1_data[4] ? register_2_q[4] : 1'bz;  // Controlled_Buffer controlled_buffer_13
  assign controlled_buffer_2_out[5] = rom_1_data[4] ? register_2_q[5] : 1'bz;  // Controlled_Buffer controlled_buffer_14
  assign controlled_buffer_2_out[6] = rom_1_data[4] ? register_2_q[6] : 1'bz;  // Controlled_Buffer controlled_buffer_15
  assign controlled_buffer_2_out[7] = rom_1_data[4] ? register_2_q[7] : 1'bz;  // Controlled_Buffer controlled_buffer_16
  inkrementor_dekrementor inkrementor_dekrementor_1 (
    ._2_0(register_2_q[0]), ._2_1(register_2_q[1]), ._2_2(register_2_q[2]), ._2_3(register_2_q[3]),
    ._2_4(register_2_q[4]), ._2_5(register_2_q[5]), ._2_6(register_2_q[6]), ._2_7(register_2_q[7]),
    .mode(rom_1_data[1]), .enable(rom_1_data[0]), .o_2_0(controlled_buffer_2_out[0]),
    .o_2_1(controlled_buffer_2_out[1]), .o_2_2(controlled_buffer_2_out[2]),
    .o_2_3(controlled_buffer_2_out[3]), .o_2_4(controlled_buffer_2_out[4]),
    .o_2_5(controlled_buffer_2_out[5]), .o_2_6(controlled_buffer_2_out[6]), .o_2_7(controlled_buffer_2_out[7]));
  mocnina mocnina_1 (
    ._2_0(register_2_q[0]), ._2_1(register_2_q[1]), ._2_2(register_2_q[2]), ._2_3(register_2_q[3]),
    ._2_4(register_2_q[4]), ._2_5(register_2_q[5]), ._2_6(register_2_q[6]), ._2_7(register_2_q[7]),
    .enable(rom_1_data[2]), .o_2_0(controlled_buffer_2_out[0]), .o_2_1(controlled_buffer_2_out[1]),
    .o_2_2(controlled_buffer_2_out[2]), .o_2_3(controlled_buffer_2_out[3]),
    .o_2_4(controlled_buffer_2_out[4]), .o_2_5(controlled_buffer_2_out[5]),
    .o_2_6(controlled_buffer_2_out[6]), .o_2_7(controlled_buffer_2_out[7]));

  // Notes on the sheet:
  //   contents of rom_1 (hex, n*v repeats v):
  //   12*9 30 28*9 30 6*9 30 30 9 9 30 66*b 30 11*b 30 20*b c b 30 7*b 30 9 9 30 5*b 30 7*b 30 66*b 30
  //   2^0
  //   2^7
  //   ie
  //   im
  //   me
  //   rl
  //   re
  //   oe
endmodule

module scitac_odcitac (
  input  a,
  input  b,
  input  m,
  output s,
  output cout
);

  wire multiplexer_1_out, not_1_out;

  not not_1 (not_1_out, a);
  xor xor_1 (s, a, b);
  Multiplexer #(.disabled(0), .enable("false")) multiplexer_1 (
    .in0(a), .in1(not_1_out), .out(multiplexer_1_out), .sel(m));
  and and_1 (cout, multiplexer_1_out, b);
endmodule

module inkrementor_dekrementor (
  input  enable,
  input  mode,
  input  _2_0,
  input  _2_1,
  input  _2_2,
  input  _2_3,
  input  _2_4,
  input  _2_5,
  input  _2_6,
  input  _2_7,
  output o_2_0,
  output o_2_1,
  output o_2_2,
  output o_2_3,
  output o_2_4,
  output o_2_5,
  output o_2_6,
  output o_2_7
);

  wire scitac_odcitac_1_cout, scitac_odcitac_1_s, scitac_odcitac_2_cout, scitac_odcitac_2_s,
       scitac_odcitac_3_cout, scitac_odcitac_3_s, scitac_odcitac_4_cout, scitac_odcitac_4_s,
       scitac_odcitac_5_cout, scitac_odcitac_5_s, scitac_odcitac_6_cout, scitac_odcitac_6_s,
       scitac_odcitac_7_cout, scitac_odcitac_7_s, scitac_odcitac_8_s;

  assign o_2_0 = enable ? scitac_odcitac_1_s : 1'bz;  // Controlled_Buffer controlled_buffer_1
  scitac_odcitac scitac_odcitac_1 (.a(_2_0), .b(1'b1), .m(mode), .cout(scitac_odcitac_1_cout), .s(scitac_odcitac_1_s));
  scitac_odcitac scitac_odcitac_2 (
    .a(_2_1), .b(scitac_odcitac_1_cout), .m(mode), .cout(scitac_odcitac_2_cout), .s(scitac_odcitac_2_s));
  assign o_2_1 = enable ? scitac_odcitac_2_s : 1'bz;  // Controlled_Buffer controlled_buffer_2
  assign o_2_2 = enable ? scitac_odcitac_3_s : 1'bz;  // Controlled_Buffer controlled_buffer_3
  scitac_odcitac scitac_odcitac_3 (
    .a(_2_2), .b(scitac_odcitac_2_cout), .m(mode), .cout(scitac_odcitac_3_cout), .s(scitac_odcitac_3_s));
  scitac_odcitac scitac_odcitac_4 (
    .a(_2_3), .b(scitac_odcitac_3_cout), .m(mode), .cout(scitac_odcitac_4_cout), .s(scitac_odcitac_4_s));
  assign o_2_3 = enable ? scitac_odcitac_4_s : 1'bz;  // Controlled_Buffer controlled_buffer_4
  scitac_odcitac scitac_odcitac_5 (
    .a(_2_4), .b(scitac_odcitac_4_cout), .m(mode), .cout(scitac_odcitac_5_cout), .s(scitac_odcitac_5_s));
  assign o_2_4 = enable ? scitac_odcitac_5_s : 1'bz;  // Controlled_Buffer controlled_buffer_5
  assign o_2_5 = enable ? scitac_odcitac_6_s : 1'bz;  // Controlled_Buffer controlled_buffer_6
  scitac_odcitac scitac_odcitac_6 (
    .a(_2_5), .b(scitac_odcitac_5_cout), .m(mode), .cout(scitac_odcitac_6_cout), .s(scitac_odcitac_6_s));
  assign o_2_6 = enable ? scitac_odcitac_7_s : 1'bz;  // Controlled_Buffer controlled_buffer_7
  scitac_odcitac scitac_odcitac_7 (
    .a(_2_6), .b(scitac_odcitac_6_cout), .m(mode), .cout(scitac_odcitac_7_cout), .s(scitac_odcitac_7_s));
  assign o_2_7 = enable ? scitac_odcitac_8_s : 1'bz;  // Controlled_Buffer controlled_buffer_8
  scitac_odcitac scitac_odcitac_8 (
    .a(_2_7), .b(scitac_odcitac_7_cout), .m(mode), .s(scitac_odcitac_8_s));  // open: cout
endmodule

module mocnina (
  input  enable,
  input  _2_0,
  input  _2_1,
  input  _2_2,
  input  _2_3,
  input  _2_4,
  input  _2_5,
  input  _2_6,
  input  _2_7,
  output o_2_0,
  output o_2_1,
  output o_2_2,
  output o_2_3,
  output o_2_4,
  output o_2_5,
  output o_2_6,
  output o_2_7
);

  wire [7:0] multiplier_1_cout, multiplier_1_out, undriven;

  Multiplier multiplier_1 (
    .a({_2_7, _2_6, _2_5, _2_4, _2_3, _2_2, _2_1, _2_0}),
    .b({_2_7, _2_6, _2_5, _2_4, _2_3, _2_2, _2_1, _2_0}), .out(multiplier_1_out), .cin(undriven),
    .cout(multiplier_1_cout));
  inkrementor_dekrementor inkrementor_dekrementor_1 (
    ._2_0(1'b1), ._2_1(1'b1), ._2_2(1'b0), ._2_3(1'b0), ._2_4(1'b0), ._2_5(1'b0), ._2_6(1'b0), ._2_7(1'b0),
    .mode(1'b0), .enable(1'b1));  // open: o_2_0, o_2_1, o_2_2, o_2_3, o_2_4, o_2_5, o_2_6, o_2_7
  assign o_2_0 = enable ? multiplier_1_out[0] : 1'bz;  // Controlled_Buffer controlled_buffer_1
  assign o_2_7 = enable ? multiplier_1_out[7] : 1'bz;  // Controlled_Buffer controlled_buffer_2
  assign o_2_1 = enable ? multiplier_1_out[1] : 1'bz;  // Controlled_Buffer controlled_buffer_3
  assign o_2_6 = enable ? multiplier_1_out[6] : 1'bz;  // Controlled_Buffer controlled_buffer_4
  assign o_2_2 = enable ? multiplier_1_out[2] : 1'bz;  // Controlled_Buffer controlled_buffer_5
  assign o_2_3 = enable ? multiplier_1_out[3] : 1'bz;  // Controlled_Buffer controlled_buffer_6
  assign o_2_4 = enable ? multiplier_1_out[4] : 1'bz;  // Controlled_Buffer controlled_buffer_7
  assign o_2_5 = enable ? multiplier_1_out[5] : 1'bz;  // Controlled_Buffer controlled_buffer_8
  // also tied to GND on the sheet: {multiplier_1_cout[0], multiplier_1_cout[1], multiplier_1_cout[2], multiplier_1_cout[3], multiplier_1_cout[4], multiplier_1_cout[5], multiplier_1_cout[6], multiplier_1_cout[7]}
endmodule
